// Digital circuit MUX.dig as structural Verilog
module MUX (
  input  D,
  input  C,
  input  B,
  input  A,
  output Y
);

  wire not_1_out;

  not not_1 (not_1_out, A);
  Multiplexer #(.Selector_Bits(3)) multiplexer_1 (
    .sel({3{A}}), .in_0(A), .in_1(A), .in_2(A), .in_3(A), .in_4(not_1_out), .in_5(not_1_out),
    .in_6(not_1_out), .in_7(not_1_out), .out(Y));

  assign B = A;
  assign C = A;
  assign D = A;

  // Notes on the sheet:
  //   Use A as the most-significant bit and 
  //   D as the least-significant bit.
  //   Converts between single bits & a 3-bit bus
endmodule

/* Test case:
A B C D Y
0 0 0 0 X
0 0 0 1 1
*/
